// Logisim project DSFProjectSimulation.circ as structural Verilog: 1 circuit, main circuit main
module main (
);

  wire and_1_out, and_2_out, and_3_out, and_4_out, and_5_out, and_6_out, and_7_out, and_8_out, and_9_out,
       and_10_out, and_11_out, and_12_out, and_13_out, and_14_out, and_15_out, and_16_out, and_17_out,
       B00_out, B01_out, B02_out, B03_out, B04_out, B05_out, B06_out, B07_out, B08_out, B09_out, d_ff_1_q,
       d_ff_2_q, d_ff_3_q, d_ff_4_q, d_ff_5_q, d_ff_6_q, d_ff_7_q, d_ff_8_q, d_ff_9_q, d_ff_10_q, E4_q,
       not_1_out, not_2_out, not_3_out, not_4_out, not_5_out, not_6_out, not_7_out, not_8_out, not_9_out,
       not_10_out, not_11_out, not_12_out, or_1_out, or_2_out, or_3_out, or_4_out, or_5_out, S0_q, S1_q,
       S4_q, undriven;

  Button B00 (.out(B00_out));
  Button B01 (.out(B01_out));
  Button B02 (.out(B02_out));
  Button B03 (.out(B03_out));
  Button B04 (.out(B04_out));
  Button B05 (.out(B05_out));
  Button B06 (.out(B06_out));
  Button B07 (.out(B07_out));
  Button B08 (.out(B08_out));
  Button B09 (.out(B09_out));
  D_Flip_Flop d_ff_1 (.D(B00_out), .clk(undriven), .Q(d_ff_1_q));  // open: Qn, preset, reset
  D_Flip_Flop d_ff_2 (.D(B01_out), .clk(undriven), .Q(d_ff_2_q));  // open: Qn, preset, reset
  D_Flip_Flop d_ff_3 (.D(B02_out), .clk(undriven), .Q(d_ff_3_q));  // open: Qn, preset, reset
  D_Flip_Flop d_ff_4 (.D(B03_out), .clk(undriven), .Q(d_ff_4_q));  // open: Qn, preset, reset
  D_Flip_Flop d_ff_5 (.D(B04_out), .clk(undriven), .Q(d_ff_5_q));  // open: Qn, preset, reset
  D_Flip_Flop d_ff_6 (.D(B05_out), .clk(undriven), .Q(d_ff_6_q));  // open: Qn, preset, reset
  D_Flip_Flop d_ff_7 (.D(B06_out), .clk(undriven), .Q(d_ff_7_q));  // open: Qn, preset, reset
  D_Flip_Flop d_ff_8 (.D(B07_out), .clk(undriven), .Q(d_ff_8_q));  // open: Qn, preset, reset
  D_Flip_Flop d_ff_9 (.D(B08_out), .clk(undriven), .Q(d_ff_9_q));  // open: Qn, preset, reset
  D_Flip_Flop d_ff_10 (.D(B09_out), .clk(undriven), .Q(d_ff_10_q));  // open: Qn, preset, reset
  not not_1 (not_1_out, d_ff_1_q);
  not not_2 (not_2_out, d_ff_2_q);
  not not_3 (not_3_out, d_ff_3_q);
  not not_4 (not_4_out, d_ff_4_q);
  not not_5 (not_5_out, d_ff_5_q);
  not not_6 (not_6_out, d_ff_6_q);
  not not_7 (not_7_out, d_ff_7_q);
  not not_8 (not_8_out, d_ff_8_q);
  not not_9 (not_9_out, d_ff_9_q);
  not not_10 (not_10_out, d_ff_10_q);
  and and_1 (and_1_out, B00_out, not_1_out);
  and and_2 (and_2_out, B01_out, not_2_out);
  and and_3 (and_3_out, B02_out, not_3_out);
  and and_4 (and_4_out, B03_out, not_4_out);
  and and_5 (and_5_out, B04_out, not_5_out);
  and and_6 (and_6_out, B05_out, not_6_out);
  and and_7 (and_7_out, B06_out, not_7_out);
  and and_8 (and_8_out, B07_out, not_8_out);
  and and_9 (and_9_out, B08_out, not_9_out);
  and and_10 (and_10_out, B09_out, not_10_out);
  or or_1 (or_1_out, and_1_out, and_2_out, and_3_out, and_4_out, and_5_out, and_6_out, and_7_out, and_8_out, and_9_out, and_10_out);
  not not_11 (not_11_out, or_1_out);
  and and_11 (and_11_out, S0_q, and_5_out);
  and and_12 (and_12_out, not_11_out, S1_q);
  or or_2 (or_2_out, and_11_out, and_12_out);
  or or_3 (or_3_out, E4_q, S4_q);
  and and_13 (and_13_out, S0_q, not_11_out);
  and and_14 (and_14_out, or_1_out, or_3_out);
  or or_4 (or_4_out, and_13_out, and_14_out);
  D_Flip_Flop S0 (.D(or_4_out), .Q(S0_q));  // open: clk, Qn, preset, reset
  D_Flip_Flop S1 (.D(or_2_out), .Q(S1_q));  // open: clk, Qn, preset, reset
  D_Flip_Flop S2 ();  // open: D, clk, Q, Qn, preset, reset
  D_Flip_Flop S3 ();  // open: D, clk, Q, Qn, preset, reset
  D_Flip_Flop S4 (.Q(S4_q));  // open: D, clk, Qn, preset, reset
  D_Flip_Flop E1 ();  // open: D, clk, Q, Qn, preset, reset
  D_Flip_Flop E2 ();  // open: D, clk, Q, Qn, preset, reset
  D_Flip_Flop E3 ();  // open: D, clk, Q, Qn, preset, reset
  D_Flip_Flop E4 (.Q(E4_q));  // open: D, clk, Qn, preset, reset
  not not_12 (not_12_out, and_2_out);
  and and_15 (and_15_out, or_1_out, not_12_out, S4_q);
  and and_16 (and_16_out, E4_q, or_1_out);
  or or_5 (or_5_out, and_15_out, and_16_out);
  and and_17 (and_17_out, S4_q, and_2_out);
  LED Red (.in(or_5_out));
  LED Green (.in(and_17_out));

  // Notes on the sheet:
  //   Press
endmodule
